# Fritzing sketch Mole Repellent (saved by Fritzing 0.9.6b)
# 18650 Li-ion Battery: CC-BY Dr Kristofer Chan, King's College London/Remote-research.org

parts:
  A1 = Waveshare esp32-c3-zero tht
  M1 = DC Motor  # not connected
  Part1 = Solar Panel [package="Renogy 50 Watts 12 Volt Monocrystalline Bendable Solar Panel"]
  A2 = CN3065 Mini Solar Charger Module
  Mod1 = 3S-BMS
  BAT1 = 18650 Li-ion Battery [package=battery-18650]
  BAT2 = 18650 Li-ion Battery [package=battery-18650]
  BAT3 = 18650 Li-ion Battery [package=battery-18650]
  U1 = Mini-360 DC-DC Buck converter [package=THT]
  Part2 = Voltage Sensor 25V
  Part3 = Dual MOSFETs PWM Module
  C1 = Capacitor [package=cap-pth-small2]
  D1 = Schottky Diode [part_number=1N5817 package="Melf DO-213 AB [SMD]"]
  S1 = Taiway 100-SP-X-T1 SPDT Miniature Toggle Switch [part_number=100-SP-X-T1-0-0-B1-M2 package=THT]

nets:
  N1: A1.Pin_2, U1.OUT-
  N2: A1.Pin_3, A2.Pin_8, A2.Pin_9, Mod1.+, U1.OUT+, Part2.VCC, Part2.+, Part3.+VIN, S1.COM
  N3: A1.Pin_6, Part3.TRIG/PWM
  N4: A1.Pin_7, Part2.S
  N5: Part1.Connector_1, A2.Pin_5
  N6: Part1.Connector_2, A2.Pin_2, A2.Pin_6, A2.Pin_7, Mod1.-, U1.IN-, Part2.GND, Part3.-VIN
  N7: Mod1.0V, BAT1.-
  N8: Mod1.4.2V, BAT1.+, BAT2.-
  N9: Mod1.8.4V, BAT2.+, BAT3.-
  N10: Mod1.12.6V, BAT3.+
  N11: U1.IN+, S1.L1
  N12: Part2.-, Part3.GND
  N13: Part3.+VLOAD, C1.2, D1.cathode
  N14: Part3.-VLOAD, C1.1, D1.anode

notes:
  12V
  3.3V or 5V step down converter
  -
  +

custom parts:
  Waveshare esp32-c3-zero tht: ESP32-C3 Mini Development Board, Based on ESP32-C3FN4 Single-core Processor, 160MHz Running Frequency, 2.4GHz Wi-Fi&Bluetooth 5.
  Solar Panel: Renogy 50 Watts 12 Volt Solar Panel
  CN3065 Mini Solar Charger Module: CN3791 MPPT Solar Panel Regulator Controller 6V 9V 12V 1 Zelle Lithium-Batterie Ladung Solar Panel Ladegerät board-Controller Module.
  3S-BMS: 3S-BMS LIPO battery charger / protection unit. Note pcb does not match the board as it will likely connect with wires, so pcb is 6 pads suitable for .1in header pins.
  18650 Li-ion Battery: 18650 li-ion Battery Standard 18650 battery with interactive connectors Creative Common Attribution 4.0 International (CC-BY 4.0) license. Any use of this part requires attribution of Dr Kristofer Chan, Department of Geography, King's College London. Contact kristofer.chan [at] kcl.ac.uk OR kris [at] remote-research.org for further information.
  Mini-360 DC-DC Buck converter: Mini-360 DC-DC Buck converter. Tiny buck step down voltage converter, input voltage 4.75 to 23V output 1 to 17V adjustable. Available from ebay and the like.
  Dual MOSFETs PWM Module: Dual Mosfet PWM Module
